# Fritzing sketch nemsensor (saved by Fritzing 0.9.3b)
breadboards: 1

parts:
  Part1 = Arduino Uno (Rev3)  # not connected
  Part2 = LCD Keypad Shield
  PCB2 = RTC_DS1302_module
  Part3 = Soil Moisture Sensor
  KY-1 = Keyes Relay [package=THT]

nets:
  N1: Part2.A5(CLK), Part3.SIG
  N2: Part2.D11_MOSI, PCB2.RST
  N3: Part2.D12_MISO, PCB2.DAT
  N4: Part2.D13_SCK, PCB2.CLK
  N5: Part2.D3, KY-1.signal
  +3V3: Part2.+3V3, PCB2.VCC
  +5V: Part2.+5V, Part3.VCC, KY-1.power
  GND: Part2.GND, PCB2.GND, Part3.GND, KY-1.ground

custom parts:
  LCD Keypad Shield: It consists of a 1602 white character blue backlight LCD. The keypad consists of 5 keys — select, up, right, down and left. To save the digital IO pins, the keypad interface uses only one ADC channel. The key value is read through a 5 stage voltage divider.
  RTC_DS1302_module: Arduino module DS1302 SPI Real Time Clock
  Keyes Relay: The Keyes 5V relay module is suitable for SCM development, home appliance control. It uses a 5V~12V TIL control signal which can control DC / AC signal.
